# Fritzing sketch schematic_atu_with_swr_meter_two_servos (saved by Fritzing 0.8.3b)
breadboards: 1

parts:
  R1 = Resistor [tolerance=±5% resistance=220 package=THT]
  R2 = Resistor [tolerance=±5% resistance=220 package=THT]
  R3 = Resistor [tolerance=±5% resistance=220 package=THT]
  ANT = Antenna  # not connected
  C1 = Ceramic Capacitor [package=THT]
  D1 = Rectifier Diode [part_number=1N34A package="300 mil [THT]"]
  R4 = Resistor [tolerance=±5% resistance=10k package=THT]
  D2 = Rectifier Diode [part_number=1N34A package="300 mil [THT]"]
  C2 = Ceramic Capacitor [package=THT]
  C3 = Ceramic Capacitor [package=THT]
  Nano1 = Arduino Nano v2.3
  L1 = Inductor [package="400 mil [THT]"]
  Part1 = Arduino BT
  R5 = Resistor [tolerance=±5% resistance=10k package=THT]
  Fine-tune_Capacitor = Basic Servo
  Main_Capacitor = Basic Servo
  U2 = RELAY [package=relay-t9a-2]
  JP1 = RCA [package=rca_lock]

nets:
  N1: R1.Pin_0, R2.Pin_0, U2.NO
  N2: R1.Pin_1, D2.anode
  N3: R3.Pin_0, C1.pin_0
  GND: R3.Pin_1, C2.pin_1, C3.pin_1, Nano1.GND, L1.pin_1, Part1.GND, Fine-tune_Capacitor.gnd, Main_Capacitor.gnd, U2.COIL1, JP1.SWITCH
  N4: C1.pin_1, D1.cathode, R4.Pin_0
  N5: D1.anode, U2.NC
  N6: R4.Pin_1, C3.pin_0, Nano1.A3
  N7: D2.cathode, C2.pin_0, R5.Pin_1
  N8: Nano1.D1TX, Part1.RX/D0
  N9: Nano1.D0RX, Part1.TX/D1
  N10: Nano1.D3, U2.COIL2
  N11: Nano1.D8, Fine-tune_Capacitor.pulse
  N12: Nano1.D9, Main_Capacitor.pulse
  N13: Nano1.A2, R5.Pin_0
  5V: Nano1.+5V, Part1.5V, Fine-tune_Capacitor.vcc, Main_Capacitor.vcc
  N14: U2.MAIN, JP1.PIN

notes:
  R1, R2 e R3 = 50 ohms
  R4 e R5 = 10K
  C1, C2 e C3 = 0,01 (ceramic 103)
  L1 is the primary loop of Magnetic Loop Antenna
  Relay (Latching relay)
  Vr
  Vf
  1) Wheatstone bridge
  2) SWR = (Vf + Vr) / (Vf - Vr)
  Auto-tune schematic for Magnetic Loop Antenna
  Por: PU2CLR - Ricardo Lima Caratti - 2/10/2013
  See program atu_two_servo_swr.ino to connect the LEDs
